// Logisim project control_logic.circ as structural Verilog: 1 circuit, main circuit control_logic
module control_logic (
  input  [31:0] inst,
  input  BrEq,
  input  BrLt,
  output PCSel,
  output RegWEn,
  output [2:0] ImmSel,
  output BrUn,
  output ASel,
  output BSel,
  output [3:0] ALUSel,
  output MemRW,
  output [1:0] WBSel,
  output CSRSel,
  output CSRWen
);

  wire and_2_out, and_3_out, and_4_out, and_5_out, and_6_out, and_7_out, and_8_out, not_1_out, not_2_out,
       not_3_out;
  wire [3:0] multiplexer_2_out, multiplexer_3_out, multiplexer_4_out, multiplexer_5_out;

  Multiplexer #(.enable("false"), .select(5), .width(4)) multiplexer_1 (
    .in0(4'b0000), .in1(4'b0110), .sel({inst[30], inst[25], inst[14:12]}));  // open: in2, in3, in4, in5, in6, in7, in8, in9, in10, in11, in12, in13, in14, in15, in16, in17, in18, in19, in20, in21, in22, in23, in24, in25, in26, in27, in28, in29, in30, in31, out
  // AND_Gate and_1 has open pins: in0=inst[6:2], in1=5'b01100, out=open
  Multiplexer #(.enable("false"), .select(3), .width(4)) multiplexer_2 (
    .in0(4'b0000), .in1(4'b0110), .in2(4'b0111), .in3(4'b1011), .in4(4'b0011), .in5(4'b0100), .in6(4'b0010),
    .in7(4'b0001), .out(multiplexer_2_out), .sel(inst[14:12]));
  not not_1 (not_1_out, inst[12]);
  not not_2 (not_2_out, inst[13]);
  not not_3 (not_3_out, inst[14]);
  and and_2 (and_2_out, inst[30], and_4_out);
  and and_3 (and_3_out, inst[25], and_4_out);
  and and_4 (and_4_out, not_1_out, not_2_out, not_3_out);
  and and_5 (and_5_out, inst[12], not_2_out, inst[14]);
  and and_6 (and_6_out, and_5_out, inst[30]);
  and and_7 (and_7_out, inst[12], inst[13], not_3_out);
  and and_8 (and_8_out, and_7_out, inst[25]);
  Multiplexer #(.enable("false"), .width(4)) multiplexer_3 (
    .in0(multiplexer_2_out), .in1(4'b1010), .out(multiplexer_3_out), .sel(and_2_out));
  Multiplexer #(.enable("false"), .width(4)) multiplexer_4 (
    .in0(multiplexer_3_out), .in1(4'b1010), .out(multiplexer_4_out), .sel(and_3_out));
  Multiplexer #(.enable("false"), .width(4)) multiplexer_5 (
    .in0(multiplexer_4_out), .in1(4'b0101), .out(multiplexer_5_out), .sel(and_6_out));
  Multiplexer #(.enable("false"), .width(4)) multiplexer_6 (
    .in0(multiplexer_5_out), .in1(4'b1011), .out(ALUSel), .sel(and_8_out));

  assign BSel = 1'b1;
  assign RegWEn = 1'b1;
  assign WBSel = 2'b01;
  // also tied to GND on the sheet: {ALUSel[0], ALUSel[1], ALUSel[2], ALUSel[3]}

  // Notes on the sheet:
  //   INPUTS to your circuit
  //   DON'T CHANGE THE LOCATIONS OF THE INPUTS AND OUTPUTS!
  //   OUTPUT from your circuit
endmodule
