// Logisim project cpu.circ as structural Verilog: 1 circuit, main circuit cpu
module cpu (
  input  clk,
  input  [31:0] INSTRUCTION,
  input  [31:0] READ_DATA,
  output [31:0] WRITE_ADDRESS,
  output [31:0] PROGRAM_COUNTER,
  output [31:0] ra,
  output [31:0] sp,
  output [31:0] t0,
  output [31:0] t1,
  output [31:0] t2,
  output [31:0] s0,
  output [31:0] s1,
  output [31:0] a0,
  output [31:0] tohost,
  output [3:0] WRITE_ENABLE,
  output [31:0] WRITE_DATA
);

  wire control_logic_1_bsel, control_logic_1_regwen;
  wire [1:0] control_logic_1_wbsel;
  wire [2:0] control_logic_1_immsel;
  wire [3:0] control_logic_1_alusel;
  wire [31:0] adder_1_out, alu_1_result, imm_gen_1_imm, multiplexer_1_out, multiplexer_2_out,
       regfile_1_read_data_1, regfile_1_read_data_2, register_1_q;

  Adder #(.width(32)) adder_1 (.a(PROGRAM_COUNTER), .b(32'h4), .out(adder_1_out));  // open: cin, cout
  Register #(.width(32)) PC (.D(adder_1_out), .clk(clk), .Q(PROGRAM_COUNTER));  // open: en, clr
  Register #(.width(32)) register_1 (.D(INSTRUCTION), .clk(clk), .Q(register_1_q));  // open: en, clr
  control_logic control_logic_1 (
    .RegWEn(control_logic_1_regwen), .ImmSel(control_logic_1_immsel), .BSel(control_logic_1_bsel),
    .ALUSel(control_logic_1_alusel), .WBSel(control_logic_1_wbsel), .inst(register_1_q));  // open: CSRWen, PCSel, BrUn, ASel, MemRW, CSRSel, BrEq, BrLt
  regfile regfile_1 (
    .rs1(register_1_q[19:15]), .rs2(register_1_q[24:20]), .rd(register_1_q[11:7]),
    .Write_Data(multiplexer_2_out), .RegWEn(control_logic_1_regwen), .clk(clk), .ra(ra), .sp(sp), .t0(t0),
    .t1(t1), .t2(t2), .s0(s0), .s1(s1), .a0(a0), .Read_Data_1(regfile_1_read_data_1),
    .Read_Data_2(regfile_1_read_data_2));
  imm_gen imm_gen_1 (.inst(register_1_q), .ImmSel(control_logic_1_immsel), .imm(imm_gen_1_imm));
  Multiplexer #(.enable("false"), .width(32)) multiplexer_1 (
    .in0(regfile_1_read_data_2), .in1(imm_gen_1_imm), .out(multiplexer_1_out), .sel(control_logic_1_bsel));
  Multiplexer #(.enable("false"), .select(2), .width(32)) multiplexer_2 (
    .in0(READ_DATA), .in1(alu_1_result), .out(multiplexer_2_out), .sel(control_logic_1_wbsel));  // open: in2, in3
  alu alu_1 (.Result(alu_1_result), .A(regfile_1_read_data_1), .B(multiplexer_1_out), .ALUSel(control_logic_1_alusel));
  csr csr_1 (.tohost(tohost));  // open: CSR_address, CSR_din, CSR_WE, clk
  // branch_comp branch_comp_1: pin names not known

  // Notes on the sheet:
  //   Output to IMEM
  //   IMEM (do **NOT** move this)
  //   Inputs from IMEM
  //   It is OK to move the PC, RegFile, ALU, MEM, Branch Comp, Imm Gen, and Control Logic to wherever is most convenient for you when constructing your CPU, and to delete this text
  //   Inputs/Outputs for testing. Do **NOT** move these.
  //   Outputs To DMEM
  //   DMEM (do **NOT** move this)
  //   Inputs From DMEM
endmodule
